# Fritzing sketch arduino+driver+motors+ir (saved by Fritzing 0.9.1b)
breadboards: 1

parts:
  part = L293D [package=THT]
  Right_Motor = DC Motor
  Left_Motor = DC Motor
  Part1 = Arduino Uno (Rev3)
  part_2 = TSOP312.., 314.. [package=THT]

nets:
  N1: part.Enable_1, part.+Vmotor, part.Enable_2, part.+V, Part1.5V, part_2.Vs
  N2: part.In_1, Part1.D12/MISO
  N3: part.Out_1_(_Controlled_by_Enable_1_), Left_Motor.pin_2
  GND: part.0V, Part1.GND, part_2.GND
  N4: part.Out_2_(_Controlled_by_Enable_1_), Left_Motor.pin_1
  N5: part.In_2, Part1.D11_PWM/MOSI
  N6: part.In_3, Part1.D9_PWM
  N7: part.Out_3_(_Controlled_by_Enable_2_), Right_Motor.pin_1
  N8: part.Out_4_(_Controlled_by_Enable_2_), Right_Motor.pin_2
  N9: part.In_4, Part1.D10_PWM/SS
  N10: Part1.D2, part_2.Data
